// Logisim project CPU_Lab_3.circ as structural Verilog
module FourBitCLA (
  input  cin,
  input  [3:0] a03,
  input  [3:0] b03,
  output [3:0] s03,
  output cout
);

  wire and_1_out, and_2_out, and_3_out, and_4_out, nand_1_out, nand_2_out, nand_3_out, nand_4_out,
       nand_5_out, nand_6_out, nand_7_out, nand_8_out, nand_9_out, nand_10_out, nand_11_out, nand_12_out,
       nand_13_out, not_1_out, not_2_out, not_3_out, not_4_out, xor_1_out, xor_2_out, xor_3_out, xor_4_out;

  and and_1 (and_1_out, a03[0], b03[0]);
  xor xor_1 (xor_1_out, a03[0], b03[0]);
  and and_2 (and_2_out, a03[1], b03[1]);
  xor xor_2 (xor_2_out, a03[1], b03[1]);
  and and_3 (and_3_out, a03[2], b03[2]);
  xor xor_3 (xor_3_out, a03[2], b03[2]);
  and and_4 (and_4_out, a03[3], b03[3]);
  xor xor_4 (xor_4_out, a03[3], b03[3]);
  xor xor_5 (s03[0], xor_1_out, cin);
  xor xor_6 (s03[1], xor_2_out, nand_11_out);
  xor xor_7 (s03[2], xor_3_out, nand_12_out);
  xor xor_8 (s03[3], xor_4_out, nand_13_out);
  not not_1 (not_1_out, and_1_out);
  not not_2 (not_2_out, and_2_out);
  nand nand_1 (nand_1_out, and_1_out, xor_2_out);
  nand nand_2 (nand_2_out, cin, xor_1_out, xor_2_out);
  not not_3 (not_3_out, and_3_out);
  nand nand_3 (nand_3_out, and_2_out, xor_3_out);
  nand nand_4 (nand_4_out, and_1_out, xor_2_out, xor_3_out);
  nand nand_5 (nand_5_out, cin, xor_1_out, xor_2_out, xor_3_out);
  nand nand_6 (nand_6_out, xor_4_out, and_3_out);
  nand nand_7 (nand_7_out, xor_4_out, xor_3_out, and_2_out);
  nand nand_8 (nand_8_out, xor_4_out, xor_3_out, xor_2_out, and_1_out);
  nand nand_9 (nand_9_out, xor_4_out, xor_3_out, xor_2_out, xor_1_out, cin);
  nand nand_10 (nand_10_out, xor_1_out, cin);
  not not_4 (not_4_out, and_4_out);
  nand nand_11 (nand_11_out, not_1_out, nand_10_out);
  nand nand_12 (nand_12_out, not_2_out, nand_1_out, nand_2_out);
  nand nand_13 (nand_13_out, not_3_out, nand_3_out, nand_4_out, nand_5_out);
  nand nand_14 (cout, not_4_out, nand_6_out, nand_7_out, nand_8_out, nand_9_out);
endmodule

module ALU (
  input  [3:0] in_1,
  input  [3:0] in_2,
  input  [3:0] in_3,
  input  [3:0] in_4,
  output [7:0] out_5
);

  wire fourbitcla_1_cout;

  FourBitCLA fourbitcla_1 (.a03(in_1), .b03(in_2), .s03(out_5[3:0]), .cout(fourbitcla_1_cout));  // open: cin
  FourBitCLA fourbitcla_2 (.cin(fourbitcla_1_cout), .a03(in_3), .b03(in_4), .s03(out_5[7:4]));  // open: cout
endmodule
